# Fritzing sketch Design1 updated (saved by Fritzing 0.9.3b)
circuit board: 5.57014cm x 1.74853cm
breadboards: 1

parts:
  Raspberry_Pi_1 = Raspberry Pi 3 [part_number=RPI-3-V1.2]
  Part1 = Adafruit I2S Mic - SPH0645 [part_number="Adafruit #3421"]

nets:
  3V3: Raspberry_Pi_1.3v3, Part1.VDD
  GND: Raspberry_Pi_1.GND, Part1.GND
  N1: Raspberry_Pi_1.GPIO19, Part1.WS
  N2: Raspberry_Pi_1.GPIO20, Part1.DATA
  N3: Raspberry_Pi_1.GPIO18, Part1.BCLK

notes:
  A. Yusuf

custom parts:
  Adafruit I2S Mic - SPH0645: For many microcontrollers, adding audio input is easy with one of our analog microphone breakouts. But as you get to bigger and better microcontrollers and microcomputers, you'll find that you don't always have an analog input, or maybe you want to avoid the noise that can seep in with an analog mic system. Once you get past 8-bit micros, you will often find an I2S peripheral, that can take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
